# Fritzing sketch assembly (saved by Fritzing 0.9.2b)
breadboards: 1

parts:
  Part1 = Arduino Uno (Rev3) - ICSP
  Part2 = Bluetooth Mate Silver
  J1 = Basic Servo
  J2 = Basic Servo
  BATT1 = 4xAA Switchable Battery Pack w/Bare Wire
  VCC1 = Battery block 9V

nets:
  N1: Part1.D4, J2.pulse
  N2: Part1.D5_PWM, J1.pulse
  N3: Part1.D6_PWM, Part2.TX_5V
  N4: Part1.D7, Part2.RX_5V
  5V: Part1.5V, Part2.VCC
  GND: Part1.GND, Part2.GND, J1.gnd, J2.gnd, BATT1.NEG, VCC1.-
  N5: Part1.VIN, VCC1.+
  VCC: J1.vcc, J2.vcc, BATT1.POS

notes:
  Right Wheel Signal - PIN 5
  Left Wheel Signal - PIN 4
  Bluetooth
  VCC from 5V
  GND to GND
  TX - PIN 6
  RX - Pin 7
  9V
  + to VIN
  - to GND
  4xAA
  + directly to Servo Power
  - to GND

custom parts:
  Bluetooth Mate Silver: Description: The Bluetooth Mate is very similar to our BlueSMiRF modem, but it is designed specifically to be used with our Arduino Pros and LilyPad Arduinos. These modems work as a serial (RX/TX) pipe, and are a great wireless replacement for serial cables. Any serial stream from 9600 to 115200bps can be passed seamlessly from your computer to your target. Bluetooth Mate has the same pin out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
  4xAA Switchable Battery Pack w/Bare Wire: 4xAA Switchable Battery Pack with Bare Wire connection
